// Logisim project circuit.circ as structural Verilog: 1 circuit, main circuit main
module main (
);

  wire and_1_out, and_2_out, and_3_out, and_4_out, and_5_out, and_6_out, and_7_out, and_8_out, and_9_out,
       and_10_out, and_11_out, Button_A_StartStop_out, Button_B_Reset_out, clock_1_out, j_k_ff_2_q,
       n7_segment_display_1_p1, n7_segment_display_1_p2, n7_segment_display_2_p3, or_1_out;
  wire [9:0] j_k_ff_1_q;

  Button Button_A_StartStop (.out(Button_A_StartStop_out));
  Button Button_B_Reset (.out(Button_B_Reset_out));
  J_K_Flip_Flop j_k_ff_1 (
    .J(1'b1), .K(1'b1), .clk(and_3_out), .Q(j_k_ff_1_q[0]), .reset(or_1_out));  // open: Qn, preset
  J_K_Flip_Flop j_k_ff_2 (
    .J(1'b1), .K(1'b1), .clk(Button_A_StartStop_out), .Q(j_k_ff_2_q), .reset(Button_B_Reset_out));  // open: Qn, preset
  and and_1 (and_1_out, 1'b1, j_k_ff_1_q[0]);
  J_K_Flip_Flop j_k_ff_3 (
    .J(and_1_out), .K(and_1_out), .clk(and_3_out), .Q(j_k_ff_1_q[1]), .reset(or_1_out));  // open: Qn, preset
  Clock clock_1 (.out(clock_1_out));
  and and_2 (and_2_out, and_1_out, j_k_ff_1_q[1]);
  J_K_Flip_Flop j_k_ff_4 (
    .J(and_2_out), .K(and_2_out), .clk(and_3_out), .Q(j_k_ff_1_q[2]), .reset(or_1_out));  // open: Qn, preset
  and and_3 (and_3_out, j_k_ff_2_q, clock_1_out);
  and and_4 (and_4_out, and_2_out, j_k_ff_1_q[2]);
  J_K_Flip_Flop j_k_ff_5 (
    .J(and_4_out), .K(and_4_out), .clk(and_3_out), .Q(j_k_ff_1_q[3]), .reset(or_1_out));  // open: Qn, preset
  or or_1 (or_1_out, Button_B_Reset_out, and_6_out);
  and and_5 (and_5_out, and_4_out, j_k_ff_1_q[3]);
  J_K_Flip_Flop j_k_ff_6 (
    .J(and_5_out), .K(and_5_out), .clk(and_3_out), .Q(j_k_ff_1_q[4]), .reset(or_1_out));  // open: Qn, preset
  and and_6 (and_6_out, j_k_ff_1_q[3], j_k_ff_1_q[4], j_k_ff_1_q[6], j_k_ff_1_q[9]);
  and and_7 (and_7_out, and_5_out, j_k_ff_1_q[4]);
  J_K_Flip_Flop j_k_ff_7 (
    .J(and_7_out), .K(and_7_out), .clk(and_3_out), .Q(j_k_ff_1_q[5]), .reset(or_1_out));  // open: Qn, preset
  and and_8 (and_8_out, and_7_out, j_k_ff_1_q[5]);
  J_K_Flip_Flop j_k_ff_8 (
    .J(and_8_out), .K(and_8_out), .clk(and_3_out), .Q(j_k_ff_1_q[6]), .reset(or_1_out));  // open: Qn, preset
  // _7_Segment_Display 7_segment_display_1: pin names not known; wires that end beside it: n7_segment_display_1_p1, n7_segment_display_1_p2
  // BCD_to_7_Segment_decoder bcd_to_7_segment_decoder_1: pin names not known
  // Binary_to_BCD_converter #(.binvalue(10)) binary_to_bcd_converter_1: pin names not known; wires that end beside it: j_k_ff_1_q, n7_segment_display_1_p1, n7_segment_display_1_p2
  and and_9 (and_9_out, and_8_out, j_k_ff_1_q[6]);
  J_K_Flip_Flop j_k_ff_9 (
    .J(and_9_out), .K(and_9_out), .clk(and_3_out), .Q(j_k_ff_1_q[7]), .reset(or_1_out));  // open: Qn, preset
  // _7_Segment_Display 7_segment_display_2: pin names not known; wires that end beside it: n7_segment_display_1_p2, 1'b1, n7_segment_display_2_p3
  // BCD_to_7_Segment_decoder bcd_to_7_segment_decoder_2: pin names not known
  and and_10 (and_10_out, and_9_out, j_k_ff_1_q[7]);
  J_K_Flip_Flop j_k_ff_10 (
    .J(and_10_out), .K(and_10_out), .clk(and_3_out), .Q(j_k_ff_1_q[8]), .reset(or_1_out));  // open: Qn, preset
  _7_Segment_Display u_7_segment_display_3 ();  // open: g, f, a, b, e, d, c, dp
  // BCD_to_7_Segment_decoder bcd_to_7_segment_decoder_3: pin names not known; wires that end beside it: n7_segment_display_2_p3
  and and_11 (and_11_out, and_10_out, j_k_ff_1_q[8]);
  J_K_Flip_Flop j_k_ff_11 (
    .J(and_11_out), .K(and_11_out), .clk(and_3_out), .Q(j_k_ff_1_q[9]), .reset(or_1_out));  // open: Qn, preset

  // Notes on the sheet:
  //   JK Flip-flop controlling
  //   clock signal propagation
  //   OR gate triggers on
  //   Reset button OR 600
  //   AND gate checks
  //   for 1001011000 (600)
endmodule
